// Logisim project Произведение.circ as structural Verilog: 1 circuit, main circuit main
module main (
  input  A1,
  input  A0,
  input  B1,
  input  B0,
  output O3,
  output O2,
  output O1,
  output O0
);

  wire and_2_out, and_3_out, and_4_out, and_5_out, and_7_out, and_8_out, not_1_out, not_2_out, not_3_out,
       not_4_out, not_5_out, xor_1_out;

  not not_1 (not_1_out, A1);
  not not_2 (not_2_out, B0);
  not not_3 (not_3_out, A0);
  not not_4 (not_4_out, B1);
  and and_1 (O3, A1, A0, B1, B0);
  not not_5 (not_5_out, A0);
  and and_2 (and_2_out, not_1_out, A0, B1);
  and and_3 (and_3_out, not_3_out, A1, B0);
  and and_4 (and_4_out, A1, not_4_out, B0);
  and and_5 (and_5_out, not_2_out, A0, B1);
  and and_6 (O0, A0, B0);
  xor xor_1 (xor_1_out, A0, B0);
  or or_1 (O1, and_2_out, and_3_out, and_4_out, and_5_out);
  and and_7 (and_7_out, xor_1_out, A1, B1);
  and and_8 (and_8_out, not_5_out, A1, B1, not_2_out);
  or or_2 (O2, and_7_out, and_8_out);
endmodule
