// Logisim project Сложение.circ as structural Verilog: 1 circuit, main circuit main
module main (
  input  A1,
  input  A0,
  input  B1,
  input  B0,
  output C2,
  output C1,
  output C0
);

  wire and_1_out, and_2_out, and_3_out, and_4_out, and_5_out, not_1_out, xor_2_out, xor_3_out, xor_4_out;

  and and_1 (and_1_out, A1, B0, A0);
  and and_2 (and_2_out, A1, B1);
  and and_3 (and_3_out, B1, A0, B0);
  or or_1 (C2, and_1_out, and_2_out, and_3_out);
  not not_1 (not_1_out, B0);
  xor xor_1 (C0, A0, B0);
  xor xor_2 (xor_2_out, A1, A0);
  xor xor_3 (xor_3_out, A1, B1);
  xor xor_4 (xor_4_out, xor_2_out, B1);
  and and_4 (and_4_out, xor_3_out, not_1_out);
  and and_5 (and_5_out, xor_4_out, B0);
  or or_2 (C1, and_4_out, and_5_out);
endmodule
