// Logisim project ЛАБ 2.circ as structural Verilog: 1 circuit, main circuit main
module main (
  input  _1,
  input  _1_2,
  input  _1_3,
  input  _2,
  input  _2_2,
  input  _2_3,
  input  _3,
  input  _3_2,
  input  _3_3,
  input  _1_4,
  input  _1_5,
  input  _1_6,
  input  _2_4,
  input  _2_5,
  input  _2_6,
  input  _3_4,
  input  _3_5,
  input  _3_6,
  output out_19,
  output out_20,
  output out_21,
  output out_22,
  output out_23,
  output out_24
);

  wire and_1_out, and_2_out, and_3_out, and_4_out, and_5_out, and_6_out, and_7_out, and_8_out, nand_1_out,
       nand_2_out, nand_3_out, nand_4_out, nand_6_out, nand_7_out, nand_8_out, nand_9_out, nand_11_out,
       nand_12_out, nand_13_out, nand_14_out, nand_15_out, nand_16_out, not_1_out, not_2_out, not_3_out,
       not_4_out, not_5_out, not_6_out;

  not not_1 (not_1_out, _2);
  and and_1 (and_1_out, _1, _3_2);
  and and_2 (and_2_out, not_1_out, _3_2);
  nand nand_1 (nand_1_out, _1_4, _3_4);
  nand nand_2 (nand_2_out, _2_4, _2_4);
  and and_3 (and_3_out, _1, not_1_out);
  nand nand_3 (nand_3_out, nand_2_out, _3_4);
  nand nand_4 (nand_4_out, nand_2_out, _1_4);
  or or_1 (out_19, and_1_out, and_3_out, and_2_out);
  nand nand_5 (out_23, nand_1_out, nand_3_out, nand_4_out);
  not not_2 (not_2_out, _2_2);
  not not_3 (not_3_out, _3_3);
  nand nand_6 (nand_6_out, _2_5, _2_5);
  nand nand_7 (nand_7_out, _3_5, _3_5);
  and and_4 (and_4_out, _1_2, not_2_out, not_3_out);
  and and_5 (and_5_out, _1_2, not_2_out, _3_3);
  nand nand_8 (nand_8_out, _1_5, nand_6_out, nand_7_out);
  nand nand_9 (nand_9_out, _1_5, nand_6_out, _3_5);
  or or_2 (out_20, and_4_out, and_5_out);
  nand nand_10 (out_22, nand_8_out, nand_9_out);
  not not_4 (not_4_out, _1_3);
  not not_5 (not_5_out, _2_3);
  not not_6 (not_6_out, _3);
  nand nand_11 (nand_11_out, _1_6, _1_6);
  nand nand_12 (nand_12_out, _2_6, _2_6);
  nand nand_13 (nand_13_out, _3_6, _3_6);
  and and_6 (and_6_out, _1_3, not_6_out);
  and and_7 (and_7_out, _1_3, not_5_out);
  and and_8 (and_8_out, not_4_out, _2_3, _3);
  nand nand_14 (nand_14_out, _1_6, nand_13_out);
  nand nand_15 (nand_15_out, _1_6, nand_12_out);
  nand nand_16 (nand_16_out, nand_11_out, _2_6, _3_6);
  or or_3 (out_21, and_6_out, and_7_out, and_8_out);
  nand nand_17 (out_24, nand_14_out, nand_15_out, nand_16_out);
endmodule
