// Logisim project DC 3.circ as structural Verilog: 1 circuit, main circuit main
module main (
  input  in_1,
  input  in_2,
  input  a0,
  input  in_4,
  input  a1,
  input  a2,
  input  in_7,
  input  a3,
  input  in_9,
  input  a4,
  input  a5,
  input  a6,
  input  in_13,
  input  in_14,
  input  a0_2,
  input  in_16,
  input  a1_2,
  input  a2_2,
  input  in_19,
  input  a3_2,
  input  in_21,
  input  a4_2,
  input  a5_2,
  input  a6_2,
  output a8,
  output a7,
  output a8_2,
  output a7_2
);

  wire not_1_out, not_2_out;

  not not_1 (not_1_out, in_9);
  not not_2 (not_2_out, in_21);
  and and_1 (a8, in_1, not_1_out);
  and and_2 (a7, in_1, in_9);
  and and_3 (a8_2, in_13, not_2_out);

  assign a7_2 = in_21;
endmodule
