// Logisim project 1.circ as structural Verilog: 1 circuit, main circuit main
module main (
  input  _0,
  input  _0_2,
  input  _1,
  input  _1_2,
  input  _2,
  input  _2_2,
  input  _3,
  input  _3_2,
  input  _0_3,
  input  _0_4,
  input  _1_3,
  input  _1_4,
  input  _2_3,
  input  _2_4,
  input  _3_3,
  output out_16,
  output out_17,
  output out_18,
  output out_19
);

  wire nand_1_out, nand_2_out, nand_3_out, nand_4_out, nand_5_out, nand_6_out, nand_7_out, nand_9_out,
       nand_10_out, nor_1_out, nor_2_out, nor_3_out, nor_4_out, nor_5_out, nor_6_out, nor_7_out, nor_8_out,
       nor_9_out, nor_10_out, nor_12_out, nor_13_out, nor_14_out, undriven;

  not nor_1 (nor_1_out, _0_2);  // NOR_Gate
  not nor_2 (nor_2_out, _1_2);  // NOR_Gate
  not nor_3 (nor_3_out, _2_2);  // NOR_Gate
  not nor_4 (nor_4_out, _3_2);  // NOR_Gate
  nand nand_1 (nand_1_out, _0_4, _0_4);
  nand nand_2 (nand_2_out, _1_4, _1_4);
  nand nand_3 (nand_3_out, _2_4, _2_4);
  nand nand_4 (nand_4_out, _3_3, _3_3);
  nor nor_5 (nor_5_out, _3_2, _1_2, _0_2);
  nor nor_6 (nor_6_out, nor_3_out, _1_2, nor_1_out);
  nor nor_7 (nor_7_out, nor_4_out, nor_2_out, nor_1_out);
  nor nor_8 (nor_8_out, _3_2, _2_2, nor_2_out);
  nand nand_5 (nand_5_out, nand_1_out, _3_3);
  nand nand_6 (nand_6_out, nand_3_out, nand_2_out, _0_4);
  nand nand_7 (nand_7_out, nand_4_out, _2_4, _1_4);
  nand nand_8 (out_19, nand_5_out, nand_6_out, nand_7_out);
  nor nor_9 (nor_9_out, nor_5_out, nor_6_out, nor_7_out);
  not nor_10 (nor_10_out, nor_9_out);  // NOR_Gate
  nor nor_11 (out_17, nor_10_out, nor_8_out, nor_8_out);
  nand nand_9 (nand_9_out, _0_3, _1_3);
  nand nand_10 (nand_10_out, nand_9_out, nand_9_out);
  nand nand_11 (out_18, nand_10_out, _2_3);
  nor nor_12 (nor_12_out, _0, _1, _2, _2);
  nor nor_13 (nor_13_out, undriven, undriven);
  not nor_14 (nor_14_out, nor_12_out);  // NOR_Gate
  // NOR_Gate nor_15 has open pins: in2=nor_13_out, out=open
  nor nor_16 (out_16, nor_14_out, _3, _3);
endmodule
