// Logisim project 2.circ as structural Verilog: 1 circuit, main circuit main
module main (
  input  R,
  input  D,
  input  C,
  input  S,
  input  S_2,
  input  S_3,
  input  C_2,
  output Q,
  output nQ
);

  wire nor_1_out, nor_2_out, nor_3_out, nor_4_out, nor_5_out, nor_6_out, nor_7_out;

  nor nor_1 (nor_1_out, S_2, S_3);
  not nor_2 (nor_2_out, D);  // NOR_Gate
  not nor_3 (nor_3_out, C);  // NOR_Gate
  nor nor_4 (nor_4_out, nor_1_out, nor_1_out);
  nor nor_5 (nor_5_out, nor_4_out, C_2);
  nor nor_6 (nor_6_out, D, nor_3_out);
  nor nor_7 (nor_7_out, nor_3_out, nor_2_out);
  nor nor_8 (Q, nor_6_out, R, nQ);
  nor nor_9 (nQ, Q, S, nor_7_out);
endmodule
