// Logisim project 3.circ as structural Verilog: 1 circuit, main circuit main
module main (
  input  X2,
  input  X1,
  input  X0,
  input  in_4,
  input  [1:0] M0_M1,
  input  Enable,
  input  Reset,
  input  M0,
  input  M1,
  input  C,
  output out_11,
  output out_12,
  output out_13
);

  wire and_1_out, multiplexer_1_out, multiplexer_2_out, multiplexer_3_out, nor_1_out, nor_2_out, nor_3_out,
       or_1_out;

  or or_1 (or_1_out, M0, M1);
  Multiplexer #(.select(2)) multiplexer_1 (
    .in0(out_11), .in1(X2), .in2(out_12), .out(multiplexer_1_out), .sel(M0_M1), .en(Enable));  // open: in3
  nor nor_1 (nor_1_out, multiplexer_1_out, multiplexer_1_out);
  and and_1 (and_1_out, or_1_out, C);
  J_K_Flip_Flop j_k_ff_1 (
    .J(multiplexer_1_out), .clk(and_1_out), .K(nor_1_out), .Q(out_11), .en(Enable), .reset(Reset));  // open: Qn, preset
  Multiplexer #(.select(2)) multiplexer_2 (
    .in0(out_12), .in1(X1), .in2(out_13), .out(multiplexer_2_out), .sel(M0_M1), .en(Enable));  // open: in3
  nor nor_2 (nor_2_out, multiplexer_2_out, multiplexer_2_out);
  J_K_Flip_Flop j_k_ff_2 (
    .J(multiplexer_2_out), .clk(and_1_out), .K(nor_2_out), .Q(out_12), .en(Enable), .reset(Reset));  // open: Qn, preset
  Multiplexer #(.select(2)) multiplexer_3 (
    .in0(out_13), .in1(X0), .in2(in_4), .out(multiplexer_3_out), .sel(M0_M1), .en(Enable));  // open: in3
  nor nor_3 (nor_3_out, multiplexer_3_out, multiplexer_3_out);
  J_K_Flip_Flop j_k_ff_3 (
    .J(multiplexer_3_out), .clk(and_1_out), .K(nor_3_out), .Q(out_13), .reset(Reset));  // open: Qn, preset, en
endmodule
