// Logisim project 3кр.circ as structural Verilog: 1 circuit, main circuit main
module main (
  input  in_1,
  input  in_2,
  input  in_3,
  input  in_4,
  input  in_5,
  input  in_6,
  output out_7,
  output out_8,
  output out_9
);

  wire multiplexer_1_out, multiplexer_2_out, multiplexer_3_out;

  Multiplexer #(.disabled(0), .enable("false")) multiplexer_1 (
    .in0(in_1), .in1(out_7), .out(multiplexer_1_out), .sel(in_4));
  D_Flip_Flop d_ff_1 (.clk(in_6), .D(multiplexer_1_out), .Q(out_7), .en(in_5));  // open: Qn, preset, reset
  Multiplexer #(.disabled(0), .enable("false")) multiplexer_2 (
    .in0(in_2), .in1(out_8), .out(multiplexer_2_out), .sel(in_4));
  D_Flip_Flop d_ff_2 (.clk(in_6), .D(multiplexer_2_out), .Q(out_8), .en(in_5));  // open: Qn, preset, reset
  Multiplexer #(.disabled(0), .enable("false")) multiplexer_3 (
    .in0(in_3), .in1(out_9), .out(multiplexer_3_out), .sel(in_4));
  D_Flip_Flop d_ff_3 (.clk(in_6), .D(multiplexer_3_out), .Q(out_9), .en(in_5));  // open: Qn, preset, reset
endmodule
