// Logisim project 4.circ as structural Verilog: 1 circuit, main circuit main
module main (
  input  in_1,
  input  in_2,
  input  in_3,
  input  in_4,
  input  in_5,
  output out_6,
  output out_7,
  output out_8,
  output out_9,
  output out_10,
  output out_11,
  output out_12,
  output [3:0] out_13,
  output [3:0] out_14
);

  wire and_1_out, and_2_out, and_3_out, and_4_out, counter_1_carry, d_ff_1_q, not_1_out, not_2_out,
       t_ff_1_qn, t_ff_2_qn, t_ff_3_qn, t_ff_4_qn, t_ff_5_qn, t_ff_6_qn;

  and and_1 (and_1_out, in_2, d_ff_1_q);
  not not_1 (not_1_out, in_2);
  not not_2 (not_2_out, d_ff_1_q);
  Counter #(.width(4), .max('hf)) counter_1 (
    .count(in_4), .Q(out_14), .carry(counter_1_carry), .clk(in_5));  // open: load, D, clr
  and and_2 (and_2_out, in_2, not_2_out);
  Counter #(.width(4), .max('hf)) counter_2 (
    .count(counter_1_carry), .Q(out_13), .clk(in_5));  // open: load, D, carry, clr
  T_Flip_Flop t_ff_1 (
    .clk(and_2_out), .T(in_1), .Q(out_12), .Qn(t_ff_1_qn), .reset(and_1_out), .en(in_3));  // open: preset
  T_Flip_Flop t_ff_2 (
    .clk(t_ff_1_qn), .T(in_1), .Q(out_11), .Qn(t_ff_2_qn), .reset(and_1_out), .en(in_3));  // open: preset
  T_Flip_Flop t_ff_3 (
    .clk(t_ff_2_qn), .T(in_1), .Q(out_10), .Qn(t_ff_3_qn), .reset(and_1_out), .en(in_3));  // open: preset
  T_Flip_Flop t_ff_4 (
    .clk(t_ff_3_qn), .T(in_1), .Q(out_9), .Qn(t_ff_4_qn), .reset(and_1_out), .en(in_3));  // open: preset
  T_Flip_Flop t_ff_5 (
    .clk(t_ff_4_qn), .T(in_1), .Q(out_8), .Qn(t_ff_5_qn), .reset(and_1_out), .en(in_3));  // open: preset
  T_Flip_Flop t_ff_6 (
    .clk(t_ff_5_qn), .T(in_1), .Q(out_7), .Qn(t_ff_6_qn), .reset(and_1_out), .en(in_3));  // open: preset
  T_Flip_Flop t_ff_7 (.clk(t_ff_6_qn), .T(in_1), .Q(out_6), .reset(and_1_out), .en(in_3));  // open: Qn, preset
  and and_3 (and_3_out, out_6, t_ff_6_qn, out_8, t_ff_4_qn);
  and and_4 (and_4_out, and_3_out, out_10, out_11, out_12);
  D_Flip_Flop #(.trigger("falling")) d_ff_1 (
    .clk(not_1_out), .D(and_4_out), .Q(d_ff_1_q), .en(in_3));  // open: Qn, preset, reset
endmodule
